// Logisim project CPU.circ as structural Verilog: 9 circuits, main circuit main
module main (
  input  reset,
  output [31:0] out_2,
  output [31:0] out_3,
  output out_4,
  output [4:0] out_5,
  output [31:0] out_6,
  output out_7,
  output [31:0] out_8,
  output [31:0] out_9
);

  wire clock, Extsle, zero;
  wire [1:0] control_1_aluop, exstyle, MemData, RegDst;
  wire [2:0] NPCsle;
  wire [31:0] Data, ext_1_b, GRF, multiplexer_3_out, next, npc_1_npc;

  Clock clock_1 (.out(clock));
  NPC npc_1 (
    .PC(out_3), .imm16(out_2[15:0]), .zero(zero), .NPC(npc_1_npc), .NPCsle(NPCsle), .GRF(GRF),
    .imm26(out_2[25:0]));
  PC PC (.Clk(clock), .Reset(reset), .npc(npc_1_npc), .DO(out_3));
  Adder #(.width(32)) adder_1 (.a(32'h4), .b(out_3), .out(next));  // open: cin, cout
  IM im_1 (.addr(out_3), .Instr(out_2));
  control control_1 (
    .NPCsle(NPCsle), .RegWrite(out_4), .ALUOp(control_1_aluop), .fuc(out_2[5:0]), .op(out_2[31:26]),
    .Extsle(Extsle), .exstyle(exstyle), .RegDst(RegDst), .MemData(MemData), .MemWrite(out_7));
  Multiplexer #(.select(2), .width(5), .enable("false")) multiplexer_1 (
    .in0(out_2[20:16]), .in1(out_2[15:11]), .in2({5{1'b1}}), .out(out_5), .sel(RegDst));  // open: in3
  Multiplexer #(.select(2), .width(32), .enable("false")) multiplexer_2 (
    .in0(out_8), .in1(Data), .in2(next), .out(out_6), .sel(MemData));  // open: in3
  EXT ext_1 (.imm16(out_2[15:0]), .Exstyle(exstyle), .B(ext_1_b));
  // Probe on ext_1_b
  GRF grf_1 (
    .A1(out_2[25:21]), .A2(out_2[20:16]), .A3(out_5), .WD(out_6), .RD1(GRF), .RD2(out_9), .clk(clock),
    .reset(reset), .WE(out_4));
  Multiplexer #(.width(32), .enable("false")) multiplexer_3 (
    .in0(out_9), .in1(ext_1_b), .out(multiplexer_3_out), .sel(Extsle));
  ALU alu_1 (.ALUOp(control_1_aluop), .A(GRF), .B(multiplexer_3_out), .out_4(out_8), .Zero(zero));  // open: Less
  DM dm_1 (.Addr(out_8), .WD(out_9), .out_6(Data), .WE(out_7), .clk(clock), .reset(reset));

  // Other names for the same wires on the sheet: Instr[31:0] = out_2; MD[31:0] = out_9; MemAddr[31:0] = out_8;
  //   MemWrite = out_7; PC[31:0] = out_3; RegAdress[4:0] = out_5; RegData[31:0] = out_6; RegWrite = out_4
endmodule

module ALU (
  input  [1:0] ALUOp,
  input  [31:0] A,
  input  [31:0] B,
  output [31:0] out_4,
  output Zero,
  output Less
);

  wire [31:0] adder_1_out, or_1_out, subtractor_1_out;

  Adder #(.width(32)) adder_1 (.a(A), .b(B), .out(adder_1_out));  // open: cin, cout
  Subtractor #(.width(32)) subtractor_1 (.a(A), .b(B), .out(subtractor_1_out));  // open: bin, bout
  assign or_1_out = A | B;  // OR_Gate or_1, 32 bits wide
  Multiplexer #(.select(2), .width(32)) multiplexer_1 (
    .in0(adder_1_out), .in1(subtractor_1_out), .in2(or_1_out), .in3({32{1'b0}}), .out(out_4), .sel(ALUOp));  // open: en
  Comparator #(.width(32), .mode("unsigned")) comparator_1 (.a(A), .b(B), .eq(Zero), .lt(Less));  // open: gt
endmodule

module GRF (
  input  WE,
  input  clk,
  input  reset,
  input  [4:0] A1,
  input  [4:0] A2,
  input  [4:0] A3,
  input  [31:0] WD,
  output [31:0] RD1,
  output [31:0] RD2
);

  wire [31:0] _1, _2, _3, _4, _5, _6, _7, _8, _9, _10, _11, _12, _13, _14, _15, _16, _17, _18, _19, _20, _21,
       _22, _23, _24, _25, _26, _27, _28, _29, _30, _31, s0, s1, s2, s3, s4, s5, s6, s7, s8, s9, s10, s11,
       s12, s13, s14, s15, s16, s17, s18, s19, s20, s21, s22, s23, s24, s25, s26, s27, s28, s29, s30, s31;

  Register #(.width(32)) register_1 (.D(s0), .clk(clk), .clr(1'b1));  // open: en, Q
  Register #(.width(32)) register_2 (.D(s1), .Q(_1), .clk(clk), .clr(reset));  // open: en
  Register #(.width(32)) register_3 (.D(s2), .Q(_2), .clk(clk), .clr(reset));  // open: en
  Register #(.width(32)) register_4 (.D(s3), .Q(_3), .clk(clk), .clr(reset));  // open: en
  Register #(.width(32)) register_5 (.D(s4), .Q(_4), .clk(clk), .clr(reset));  // open: en
  Register #(.width(32)) register_6 (.D(s5), .Q(_5), .clk(clk), .clr(reset));  // open: en
  Register #(.width(32)) register_7 (.D(s6), .Q(_6), .clk(clk), .clr(reset));  // open: en
  Register #(.width(32)) register_8 (.D(s7), .Q(_7), .clk(clk), .clr(reset));  // open: en
  Demultiplexer #(.select(5), .width(32), .tristate("true")) demultiplexer_1 (
    .out0(s0), .out1(s1), .out2(s2), .out3(s3), .out4(s4), .out5(s5), .out6(s6), .out7(s7), .out8(s8),
    .out9(s9), .out10(s10), .out11(s11), .out12(s12), .out13(s13), .out14(s14), .out15(s15), .out16(s16),
    .out17(s17), .out18(s18), .out19(s19), .out20(s20), .out21(s21), .out22(s22), .out23(s23), .out24(s24),
    .out25(s25), .out26(s26), .out27(s27), .out28(s28), .out29(s29), .out30(s30), .out31(s31), .in(WD),
    .sel(A3), .en(WE));
  Register #(.width(32)) register_9 (.D(s8), .Q(_8), .clk(clk), .clr(reset));  // open: en
  Register #(.width(32)) register_10 (.D(s9), .Q(_9), .clk(clk), .clr(reset));  // open: en
  Register #(.width(32)) register_11 (.D(s10), .Q(_10), .clk(clk), .clr(reset));  // open: en
  Register #(.width(32)) register_12 (.D(s11), .Q(_11), .clk(clk), .clr(reset));  // open: en
  Register #(.width(32)) register_13 (.D(s12), .Q(_12), .clk(clk), .clr(reset));  // open: en
  Register #(.width(32)) register_14 (.D(s13), .Q(_13), .clk(clk), .clr(reset));  // open: en
  Register #(.width(32)) register_15 (.D(s14), .Q(_14), .clk(clk), .clr(reset));  // open: en
  Register #(.width(32)) register_16 (.D(s15), .Q(_15), .clk(clk), .clr(reset));  // open: en
  Register #(.width(32)) register_17 (.D(s16), .Q(_16), .clk(clk), .clr(reset));  // open: en
  Register #(.width(32)) register_18 (.D(s17), .Q(_17), .clk(clk), .clr(reset));  // open: en
  Register #(.width(32)) register_19 (.D(s18), .Q(_18), .clk(clk), .clr(reset));  // open: en
  Register #(.width(32)) register_20 (.D(s19), .Q(_19), .clk(clk), .clr(reset));  // open: en
  Register #(.width(32)) register_21 (.D(s20), .Q(_20), .clk(clk), .clr(reset));  // open: en
  Register #(.width(32)) register_22 (.D(s21), .Q(_21), .clk(clk), .clr(reset));  // open: en
  Register #(.width(32)) register_23 (.D(s22), .Q(_22), .clk(clk), .clr(reset));  // open: en
  Register #(.width(32)) register_24 (.D(s23), .Q(_23), .clk(clk), .clr(reset));  // open: en
  Register #(.width(32)) register_25 (.D(s24), .Q(_24), .clk(clk), .clr(reset));  // open: en
  Register #(.width(32)) register_26 (.D(s25), .Q(_25), .clk(clk), .clr(reset));  // open: en
  Register #(.width(32)) register_27 (.D(s26), .Q(_26), .clk(clk), .clr(reset));  // open: en
  Register #(.width(32)) register_28 (.D(s27), .Q(_27), .clk(clk), .clr(reset));  // open: en
  Register #(.width(32)) register_29 (.D(s28), .Q(_28), .clk(clk), .clr(reset));  // open: en
  Register #(.width(32)) register_30 (.D(s29), .Q(_29), .clk(clk), .clr(reset));  // open: en
  Register #(.width(32)) register_31 (.D(s30), .Q(_30), .clk(clk), .clr(reset));  // open: en
  Register #(.width(32)) register_32 (.D(s31), .Q(_31), .clk(clk), .clr(reset));  // open: en
  Multiplexer #(.select(5), .width(32), .enable("false")) multiplexer_1 (
    .in0({32{1'b0}}), .in1(_1), .in2(_2), .in3(_3), .in4(_4), .in5(_5), .in6(_6), .in7(_7), .in8(_8),
    .in9(_9), .in10(_10), .in11(_11), .in12(_12), .in13(_13), .in14(_14), .in15(_15), .in16(_16), .in17(_17),
    .in18(_18), .in19(_19), .in20(_20), .in21(_21), .in22(_22), .in23(_23), .in24(_24), .in25(_25),
    .in26(_26), .in27(_27), .in28(_28), .in29(_29), .in30(_30), .in31(_31), .out(RD1), .sel(A1));
  Multiplexer #(.select(5), .width(32), .enable("false")) multiplexer_2 (
    .in0({32{1'b0}}), .in1(_1), .in2(_2), .in3(_3), .in4(_4), .in5(_5), .in6(_6), .in7(_7), .in8(_8),
    .in9(_9), .in10(_10), .in11(_11), .in12(_12), .in13(_13), .in14(_14), .in15(_15), .in16(_16), .in17(_17),
    .in18(_18), .in19(_19), .in20(_20), .in21(_21), .in22(_22), .in23(_23), .in24(_24), .in25(_25),
    .in26(_26), .in27(_27), .in28(_28), .in29(_29), .in30(_30), .in31(_31), .out(RD2), .sel(A2));
endmodule

module EXT (
  input  [15:0] imm16,
  input  [1:0] Exstyle,
  output [31:0] B
);

  wire [15:0] bit_extender_1_out;
  wire [31:0] bit_extender_2_out, bit_extender_3_out;

  assign bit_extender_1_out = {{15{1'b0}}, 1'b0};  // Bit_Extender bit_extender_1
  assign bit_extender_2_out = {{16{imm16[15]}}, imm16};  // Bit_Extender bit_extender_2
  assign bit_extender_3_out = {{16{1'b0}}, imm16};  // Bit_Extender bit_extender_3
  Multiplexer #(.select(2), .width(32)) multiplexer_1 (
    .in0(bit_extender_2_out), .in1(bit_extender_3_out), .in2({imm16, bit_extender_1_out}), .out(B),
    .sel(Exstyle));  // open: in3, en
endmodule

module PC (
  input  Clk,
  input  Reset,
  input  [31:0] npc,
  output [31:0] DO
);

  wire [31:0] register_1_q, xor_1_out;

  assign xor_1_out = 32'h3000 ^ npc;  // XOR_Gate xor_1, 32 bits wide
  Register #(.width(32)) register_1 (.D(xor_1_out), .Q(register_1_q), .clk(Clk), .clr(Reset));  // open: en
  assign DO = 32'h3000 ^ register_1_q;  // XOR_Gate xor_2, 32 bits wide
endmodule

module NPC (
  input  [31:0] PC,
  input  [25:0] imm26,
  input  [31:0] GRF,
  input  [15:0] imm16,
  input  [2:0] NPCsle,
  input  zero,
  output [31:0] NPC
);

  wire [31:0] adder_1_out, adder_2_out, bit_extender_1_out, multiplexer_1_out;

  Adder #(.width(32)) adder_1 (.a(32'h4), .b(PC), .out(adder_1_out));  // open: cin, cout
  assign bit_extender_1_out = {{14{imm16[15]}}, {imm16, 2'b00}};  // Bit_Extender bit_extender_1
  Adder #(.width(32)) adder_2 (.a(adder_1_out), .b(bit_extender_1_out), .out(adder_2_out));  // open: cin, cout
  Multiplexer #(.width(32), .enable("false")) multiplexer_1 (
    .in0(adder_1_out), .in1(adder_2_out), .out(multiplexer_1_out), .sel(zero));
  Multiplexer #(.select(3), .width(32), .enable("false")) multiplexer_2 (
    .in0(adder_1_out), .in1({PC[31:28], imm26, 2'b00}), .in2(GRF), .in3(multiplexer_1_out), .out(NPC),
    .sel(NPCsle));  // open: in4, in5, in6, in7
endmodule

module IM (
  input  [31:0] addr,
  output [31:0] Instr
);

  wire [31:0] subtractor_1_out;

  Subtractor #(.width(32)) subtractor_1 (.a(addr), .b(32'h3000), .out(subtractor_1_out));  // open: bin, bout
  ROM #(.addrWidth(12), .dataWidth(32)) rom_1 (.addr(subtractor_1_out[13:2]), .data(Instr));  // open: sel

  // Notes on the sheet:
  //   contents of rom_1 (hex, n*v repeats v):
  //   340a0016 34120012 3413001f 34040000 340f0014 34030012 34110018 34090002 36d07fad ac65ffcc 8e75ff84
  //   6c1022 12ce0001 11aa820 30ba022 14bd820 352562ac e03820 0 132d0008 26cc820 24ed022 8c80005c 330c822
  //   0 3c0e76aa 11aa022 0 adf1ffc8 10f80002 8d350010 363a31c1
endmodule

module DM (
  input  [31:0] Addr,
  input  WE,
  input  clk,
  input  reset,
  input  [31:0] WD,
  output [31:0] out_6
);

  RAM #(.addrWidth(12), .dataWidth(32), .bus("separate")) ram_1 (
    .addr(Addr[13:2]), .din(WD), .data(out_6), .str(WE), .clk(clk), .clr(reset));  // open: sel, ld
endmodule

module control (
  input  [5:0] fuc,
  input  [5:0] op,
  output Extsle,
  output [1:0] exstyle,
  output RegWrite,
  output [1:0] RegDst,
  output [2:0] NPCsle,
  output [1:0] ALUOp,
  output MemWrite,
  output [1:0] MemData
);

  wire add, beq, j, jr, lui, lw, nop, not_1_out, not_2_out, not_3_out, not_4_out, not_5_out, not_6_out,
       not_7_out, not_8_out, not_9_out, not_10_out, not_11_out, not_12_out, ori, sub, sw;

  not not_1 (not_1_out, op[5]);
  not not_2 (not_2_out, op[3]);
  not not_3 (not_3_out, op[4]);
  not not_4 (not_4_out, op[2]);
  not not_5 (not_5_out, op[1]);
  not not_6 (not_6_out, fuc[5]);
  not not_7 (not_7_out, op[0]);
  not not_8 (not_8_out, fuc[3]);
  not not_9 (not_9_out, fuc[4]);
  not not_10 (not_10_out, fuc[1]);
  not not_11 (not_11_out, fuc[2]);
  not not_12 (not_12_out, fuc[0]);
  and u_add (add, not_1_out, not_3_out, not_2_out, not_4_out, not_5_out, not_7_out, fuc[5], not_9_out, not_8_out, not_11_out, not_10_out, not_12_out);
  and u_sub (sub, not_1_out, not_3_out, not_2_out, not_4_out, not_5_out, not_7_out, fuc[5], not_9_out, not_8_out, not_11_out, fuc[1], not_12_out);
  and u_beq (beq, not_1_out, not_3_out, not_2_out, op[2], not_5_out, not_7_out);
  and u_lw (lw, op[5], not_3_out, not_2_out, not_4_out, op[1], op[0]);
  and u_sw (sw, op[5], not_3_out, op[3], not_4_out, op[1], op[0]);
  and u_ori (ori, not_1_out, not_3_out, op[3], op[2], not_5_out, op[0]);
  and u_lui (lui, not_1_out, not_3_out, op[3], op[2], op[1], op[0]);
  and u_nop (nop, not_1_out, not_3_out, not_2_out, not_4_out, not_5_out, not_7_out);
  and and_1 (RegDst[1], not_1_out, not_3_out, not_2_out, not_4_out, op[1], op[0]);
  and and_2 (j, not_1_out, not_3_out, not_2_out, not_4_out, op[1], not_7_out);
  and and_3 (jr, not_1_out, not_3_out, not_2_out, not_4_out, not_5_out, not_7_out, not_6_out, not_9_out, fuc[3], not_11_out, not_10_out, not_12_out);
  // AND_Gate and_4 is placed but not wired
  buf or_1 (NPCsle[2], 1'b0);  // OR_Gate
  or or_2 (NPCsle[1], beq, jr);
  or or_3 (NPCsle[0], beq, j, RegDst[1]);
  or u_Regwrite (RegWrite, lui, ori, lw, sub, add);
  buf or_4 (ALUOp[0], sub);  // OR_Gate
  buf or_5 (ALUOp[1], ori);  // OR_Gate
  or or_6 (Extsle, lw, lui, sw, ori);
  buf or_7 (exstyle[1], lui);  // OR_Gate
  buf or_8 (exstyle[0], ori);  // OR_Gate
  or or_9 (RegDst[0], sub, add);
  buf or_10 (MemData[1], RegDst[1]);  // OR_Gate
  buf or_11 (MemData[0], lw);  // OR_Gate
  buf or_12 (MemWrite, sw);  // OR_Gate

  // Other names for the same wires on the sheet: jal = RegDst[1]
endmodule
